// Logisim project Project.circ as structural Verilog: 10 circuits, main circuit main
module main (
  input  EN,
  input  in_2,
  input  in_3,
  input  in_4,
  output [7:0] out_5
);

  wire and_2_out, and_3_out, Carry, cdm_8_mark5_1_p4, cdm_8_mark5_1_p5, cdm_8_mark5_1_p7, cdm_8_mark5_1_p8,
       cdm_8_mark5_1_p10, cdm_8_mark5_1_p11, cdm_8_mark5_1_p12, Clock, Clock_1, Clock_2, comparator_1_eq,
       comparator_2_eq, comparator_3_eq, comparator_4_gt, controlled_buffer_3_out, controlunit_1_en_2,
       d_ff_1_q, decoder_1_out0, decoder_1_out1, IAck, IOsel, IRQ, multiplexer_1_out, multiplexer_6_out,
       not_1_out, not_2_out, not_3_out, not_4_out, or_1_out, RAM, register_2_q, Reset, videochip_1_en_2,
       videochip_2_en_2, videochip_3_en_2, VX, VY;
  wire [1:0] videochip_1_id_2, videochip_2_id_2, videochip_3_id_2;
  wire [2:0] cnt, vec;
  wire [3:0] joystick_1_y;
  wire [4:0] BallX, BallY, controlunit_1_leftbaty_2, controlunit_1_rigthbaty, videochip_1_ballx_2,
       videochip_1_bally_2, videochip_1_leftbaty_2, videochip_1_rightbaty_2, videochip_2_ballx_2,
       videochip_2_bally_2, videochip_2_leftbaty_2, videochip_2_rightbaty_2, videochip_3_ballx_2,
       videochip_3_bally_2, videochip_3_leftbaty_2, videochip_3_rightbaty_2;
  wire [7:0] Addr, Address, cdm_8_mark5_1_p14, cdm_8_mark5_1_p15, enS, IOdat, multiplexer_3_out,
       multiplexer_4_out, multiplexer_5_out, myS, PC, register_1_q;
  wire [7:7] BallX_8, BallY_8, VX_8, VY_8;
  wire [31:0] videochip_1_out_7, videochip_1_out_10, videochip_1_out_12, videochip_1_out_15,
       videochip_1_out_17, videochip_1_out_18, videochip_1_out_19, videochip_1_out_20, videochip_2_out_7,
       videochip_2_out_10, videochip_2_out_12, videochip_2_out_15, videochip_2_out_17, videochip_2_out_18,
       videochip_2_out_19, videochip_2_out_20, videochip_3_out_7, videochip_3_out_10, videochip_3_out_12,
       videochip_3_out_15, videochip_3_out_17, videochip_3_out_18, videochip_3_out_19, videochip_3_out_20,
       videochip_4_out_7, videochip_4_out_10, videochip_4_out_12, videochip_4_out_15, videochip_4_out_17,
       videochip_4_out_18, videochip_4_out_19, videochip_4_out_20;

  Pull_Resistor pull_resistor_1 (.node(VX_8[7]));
  Pull_Resistor pull_resistor_2 (.node(VY_8[7]));
  Pull_Resistor pull_resistor_3 (.node(BallX_8[7]));
  Pull_Resistor pull_resistor_4 (.node(BallY_8[7]));
  // Probe on cdm_8_mark5_1_p4
  // Debugger debugger_1: pin names not known
  // Probe on cdm_8_mark5_1_p8
  // Probe on cdm_8_mark5_1_p7
  // Probe on cdm_8_mark5_1_p5
  // Probe on PC
  Multiplexer multiplexer_1 (.in0(1'b0), .in1(Clock_1), .out(multiplexer_1_out), .sel(RAM), .en(Carry));
  Decoder #(.disabled(0)) decoder_1 (
    .out0(decoder_1_out0), .out1(decoder_1_out1), .sel(cdm_8_mark5_1_p10), .en(cdm_8_mark5_1_p11));
  // CdM_8_mark5 cdm_8_mark5_1: pin names not known; wires that end beside it: IRQ, vec, IAck, cdm_8_mark5_1_p4, cdm_8_mark5_1_p5, multiplexer_1_out, cdm_8_mark5_1_p7, cdm_8_mark5_1_p8, PC, cdm_8_mark5_1_p10, cdm_8_mark5_1_p11, cdm_8_mark5_1_p12, Address, cdm_8_mark5_1_p14, cdm_8_mark5_1_p15
  Multiplexer #(.enable("false")) multiplexer_2 (.in0(Clock_1), .in1(1'b0), .out(Clock_2), .sel(d_ff_1_q));
  Multiplexer #(.select(3), .width(8), .enable("false")) multiplexer_3 (
    .in0(out_5), .in1({{3{BallX_8[7]}}, BallX}), .in2({{3{BallY_8[7]}}, BallY}), .in3({{7{VX_8[7]}}, VX}),
    .in4({{7{VY_8[7]}}, VY}), .in5(IOdat), .out(multiplexer_3_out), .sel(cnt));  // open: in6, in7
  and and_1 (IOsel, Address[4], Address[5], Address[6], Address[7], decoder_1_out1);
  not not_1 (not_1_out, cdm_8_mark5_1_p12);
  assign IOdat = not_1_out ? cdm_8_mark5_1_p14 : 8'bz;  // Controlled_Buffer controlled_buffer_1
  assign cdm_8_mark5_1_p15 = cdm_8_mark5_1_p12 ? IOdat : 8'bz;  // Controlled_Buffer controlled_buffer_2
  D_Flip_Flop d_ff_1 (.clk(Carry), .D(Carry), .Q(d_ff_1_q), .reset(comparator_1_eq));  // open: Qn, preset, en
  Multiplexer #(.width(8), .enable("false")) multiplexer_4 (
    .in0(Addr), .in1(Address), .out(multiplexer_4_out), .sel(and_2_out));
  and and_2 (and_2_out, RAM, Carry);
  and and_3 (and_3_out, decoder_1_out1, ~IOsel);  // AND_Gate
  Comparator comparator_1 (.a(PC), .b(8'h2b), .eq(comparator_1_eq));  // open: gt, lt
  D_Flip_Flop #(.trigger("high")) d_ff_2 (.clk(d_ff_1_q), .D(d_ff_1_q), .Q(RAM));  // open: Qn, preset, en, reset
  Register register_1 (.D(IOdat), .Q(register_1_q), .clk(comparator_2_eq));  // open: en, clr
  Comparator comparator_2 (.a(8'hf1), .b(Address), .eq(comparator_2_eq));  // open: gt, lt
  not not_2 (not_2_out, register_2_q);
  Register #(.width(1)) register_2 (
    .D(not_2_out), .Q(register_2_q), .clk(comparator_1_eq), .clr(not_3_out));  // open: en
  not not_3 (not_3_out, Carry);
  Multiplexer #(.width(8), .enable("false")) multiplexer_5 (
    .in1(register_1_q), .out(multiplexer_5_out), .sel(comparator_3_eq));  // open: in0
  Comparator #(.width(1)) comparator_3 (.a(1'b1), .b(VX), .eq(comparator_3_eq));  // open: gt, lt
  not not_4 (not_4_out, Clock_1);
  Multiplexer #(.enable("false")) multiplexer_6 (
    .in0(1'b0), .in1(cdm_8_mark5_1_p12), .out(multiplexer_6_out), .sel(Carry));
  or or_1 (or_1_out, and_3_out, ~Carry);  // OR_Gate
  Counter #(.width(3), .max('h7)) counter_1 (
    .Q(cnt), .carry(Carry), .clk(Clock_2), .clr(controlled_buffer_3_out));  // open: load, D, count
  assign controlled_buffer_3_out = Carry ? register_2_q : 1'bz;  // Controlled_Buffer controlled_buffer_3
  Hex_Digit_Display hex_digit_display_1 (.value(myS[3:0]));  // open: dp
  Joystick joystick_1 (.y(joystick_1_y));  // open: x
  Multiplexer #(.width(8), .enable("false")) multiplexer_7 (
    .in1(multiplexer_5_out), .out(out_5), .sel(comparator_4_gt));  // open: in0
  Comparator #(.width(5)) comparator_4 (.a(BallX), .b({5{1'b0}}), .gt(comparator_4_gt));  // open: eq, lt
  RAM #(.bus("separate")) ram_1 (
    .addr(multiplexer_4_out), .din(multiplexer_3_out), .data(IOdat), .sel(or_1_out), .clk(not_4_out),
    .ld(multiplexer_6_out), .clr(Reset));  // open: str
  ROM rom_1 (.addr(Address), .data(IOdat), .sel(decoder_1_out0));
  Hex_Digit_Display hex_digit_display_2 (.value(myS[7:4]));  // open: dp
  Clock u_Clock (.out(Clock));
  ControlUnit controlunit_1 (
    .EN(EN), .Clock(Clock), .LeftBatY(joystick_1_y), .RightBatY(out_5[3:0]), .Reset(Reset),
    .EN_2(controlunit_1_en_2), .EnemyScore(enS), .MyScore(myS), .RigthBatY(controlunit_1_rigthbaty),
    .LeftBatY_2(controlunit_1_leftbaty_2), .BallX(BallX), .BallY(BallY), ._1_2(in_2), ._1_4(in_3),
    ._1_8(in_4), .VX(VX), .VY(VY));
  DotMatrix #(.matrixcols(32), .matrixrows(32)) dotmatrix_1 (
    .col0(videochip_1_out_7), .col1(videochip_1_out_10), .col2(videochip_1_out_12),
    .col3(videochip_1_out_15), .col4(videochip_1_out_17), .col5(videochip_1_out_18),
    .col6(videochip_1_out_19), .col7(videochip_1_out_20), .col8(videochip_2_out_7),
    .col9(videochip_2_out_10), .col10(videochip_2_out_12), .col11(videochip_2_out_15),
    .col12(videochip_2_out_17), .col13(videochip_2_out_18), .col14(videochip_2_out_19),
    .col15(videochip_2_out_20), .col16(videochip_3_out_7), .col17(videochip_3_out_10),
    .col18(videochip_3_out_12), .col19(videochip_3_out_15), .col20(videochip_3_out_17),
    .col21(videochip_3_out_18), .col22(videochip_3_out_19), .col23(videochip_3_out_20),
    .col24(videochip_4_out_7), .col25(videochip_4_out_10), .col26(videochip_4_out_12),
    .col27(videochip_4_out_15), .col28(videochip_4_out_17), .col29(videochip_4_out_18),
    .col30(videochip_4_out_19), .col31(videochip_4_out_20));
  Pull_Resistor pull_resistor_5 (.node(Clock_1));
  assign Clock_1 = EN ? Clock : 1'bz;  // Controlled_Buffer controlled_buffer_4
  Multiplexer #(.select(3), .width(8), .enable("false")) multiplexer_8 (
    .in0(8'hf0), .in1(8'hf1), .in2(8'hf2), .in3(8'hf3), .in4(8'hf4), .out(Addr), .sel(cnt));  // open: in5, in6, in7
  VideoChip videochip_1 (
    .ballY(BallY), .out_7(videochip_1_out_7), .out_10(videochip_1_out_10), .out_12(videochip_1_out_12),
    .out_15(videochip_1_out_15), .out_17(videochip_1_out_17), .out_18(videochip_1_out_18),
    .out_19(videochip_1_out_19), .out_20(videochip_1_out_20), .EN(controlunit_1_en_2),
    .EN_2(videochip_1_en_2), .ballX(BallX), .ballY_2(videochip_1_bally_2), .ballX_2(videochip_1_ballx_2),
    .ID_2(videochip_1_id_2), .LeftBatY(controlunit_1_leftbaty_2), .RightBatY(controlunit_1_rigthbaty),
    .LeftBatY_2(videochip_1_leftbaty_2), .RightBatY_2(videochip_1_rightbaty_2));  // open: ID
  VideoChip videochip_2 (
    .ballY(videochip_1_bally_2), .out_7(videochip_2_out_7), .out_10(videochip_2_out_10),
    .out_12(videochip_2_out_12), .out_15(videochip_2_out_15), .out_17(videochip_2_out_17),
    .out_18(videochip_2_out_18), .out_19(videochip_2_out_19), .out_20(videochip_2_out_20),
    .EN(videochip_1_en_2), .EN_2(videochip_2_en_2), .ballX(videochip_1_ballx_2),
    .ballY_2(videochip_2_bally_2), .ballX_2(videochip_2_ballx_2), .ID_2(videochip_2_id_2),
    .LeftBatY(videochip_1_leftbaty_2), .RightBatY(videochip_1_rightbaty_2),
    .LeftBatY_2(videochip_2_leftbaty_2), .RightBatY_2(videochip_2_rightbaty_2), .ID(videochip_1_id_2));
  VideoChip videochip_3 (
    .ballY(videochip_2_bally_2), .out_7(videochip_3_out_7), .out_10(videochip_3_out_10),
    .out_12(videochip_3_out_12), .out_15(videochip_3_out_15), .out_17(videochip_3_out_17),
    .out_18(videochip_3_out_18), .out_19(videochip_3_out_19), .out_20(videochip_3_out_20),
    .EN(videochip_2_en_2), .EN_2(videochip_3_en_2), .ballX(videochip_2_ballx_2),
    .ballY_2(videochip_3_bally_2), .ballX_2(videochip_3_ballx_2), .ID_2(videochip_3_id_2),
    .LeftBatY(videochip_2_leftbaty_2), .RightBatY(videochip_2_rightbaty_2),
    .LeftBatY_2(videochip_3_leftbaty_2), .RightBatY_2(videochip_3_rightbaty_2), .ID(videochip_2_id_2));
  VideoChip videochip_4 (
    .ballY(videochip_3_bally_2), .out_7(videochip_4_out_7), .out_10(videochip_4_out_10),
    .out_12(videochip_4_out_12), .out_15(videochip_4_out_15), .out_17(videochip_4_out_17),
    .out_18(videochip_4_out_18), .out_19(videochip_4_out_19), .out_20(videochip_4_out_20),
    .EN(videochip_3_en_2), .ballX(videochip_3_ballx_2), .LeftBatY(videochip_3_leftbaty_2),
    .RightBatY(videochip_3_rightbaty_2), .ID(videochip_3_id_2));  // open: EN_2, ballY_2, ballX_2, ID_2, LeftBatY_2, RightBatY_2
  Hex_Digit_Display hex_digit_display_3 (.value(enS[3:0]));  // open: dp
  Hex_Digit_Display hex_digit_display_4 (.value(enS[7:4]));  // open: dp
  Button R (.out(Reset));

  // Other names for the same wires on the sheet: _1_2 = in_2; _1_4 = in_3; _1_8 = in_4; IOaddr[3:0] = Address[3:0];
  //   BallX_8[6:0] = {{2{BallX_8[7]}}, BallX}; BallY_8[6:0] = {{2{BallY_8[7]}}, BallY}; RightBatY_8[7:0] = out_5;
  //   VX_8[6:0] = {{6{VX_8[7]}}, VX}; VY_8[6:0] = {{6{VY_8[7]}}, VY}

  // Notes on the sheet:
  //   Turn on the game!
  //   Recommended mode 
  //   → 
  //   0
  //   1)
  //   1
  //   2)
  //   1
  //   3)
  //   1
  //   4)
  //   0
  //   0
  //   0
  //   0
  //   1
  //   0
  //   1
  //   1
  //   Here you can change the ball speed
  //   Several options for changes
  //   -  The ball moves every tick
  //   -  The ball moves 1 time in 2 ticks 
  //   -  The ball moves 1 time in 4 ticks 
  //   -  The ball moves 1 time in 8 ticks 
  //   contents of rom_1 (hex, n*v repeats v):
  //   cd e0 d1 f1 b5 d3 f3 bf f e0 e 5 e1 10 ee 2b d0 f0 31 5 99 d3 f4 bf f e1 1c 8d d2 f2 ba 19 e3 25 d2
  //   ff 36 d3 ff 3e d0 f0 a2 ee 2 d7 d4
  //   Your score
  //   Enemy score
endmodule

module ControlUnit (
  input  EN,
  input  Clock,
  input  _1_2,
  input  _1_4,
  input  _1_8,
  input  [3:0] LeftBatY,
  input  [3:0] RightBatY,
  input  Reset,
  output EN_2,
  output [4:0] BallX,
  output [4:0] BallY,
  output [7:0] EnemyScore,
  output [7:0] MyScore,
  output [4:0] LeftBatY_2,
  output [4:0] RigthBatY,
  output VX,
  output VY
);

  wire and_1_out, and_2_out, and_3_out, and_4_out, BotWallReflect, BT, comparator_1_eq, comparator_2_eq,
       EN_t, LeftBatReflect, LeftWallReflect, or_2_out, or_3_out, pull_resistor_1_node, RightBatReflect,
       RightWallReflect, TopWallReflect, VX_qn, VY_qn;
  wire [4:0] adder_1_out, adder_2_out, CoordToReflectX, CoordToReflectY, subtractor_1_out, subtractor_2_out;

  or or_1 (EN_t, Reset, ~EN);  // OR_Gate
  LeftBatMovement leftbatmovement_1 (.EN(EN_t), .Clock(Clock), .LeftBatY(LeftBatY), .out_4(LeftBatY_2));
  Comparator #(.width(5), .mode("unsigned")) comparator_1 (
    .a({5{1'b0}}), .b(BallX), .eq(comparator_1_eq));  // open: gt, lt
  Comparator #(.width(5), .mode("unsigned")) comparator_2 (
    .a({5{1'b1}}), .b(BallX), .eq(comparator_2_eq));  // open: gt, lt
  and and_1 (and_1_out, ~VX, comparator_1_eq);  // AND_Gate
  and and_2 (and_2_out, VX, comparator_2_eq);
  Counter #(.width(5), .max('h1f)) BatY (
    .load(and_4_out), .Q(RigthBatY), .clk(pull_resistor_1_node), .clr(EN_t));  // open: D, count, carry
  Pull_Resistor pull_resistor_1 (.node(pull_resistor_1_node));
  buf buffer_1 (pull_resistor_1_node, and_4_out);
  buf buffer_2 (pull_resistor_1_node, and_3_out);
  and and_3 (and_3_out, ~RightBatY[3], ~RightBatY[2], ~RightBatY[1], RightBatY[0], Clock);  // AND_Gate
  ScoreCounter scorecounter_1 (.Flag(and_1_out), .Reset(EN_t), .Score(EnemyScore));
  ScoreCounter scorecounter_2 (.Flag(and_2_out), .Reset(EN_t), .Score(MyScore));
  BallDelay balldelay_1 (.Clock(Clock), .in_2(_1_2), .in_3(_1_4), .in_4(_1_8), .out_5(BT));
  and and_4 (and_4_out, RightBatY[0], RightBatY[1], RightBatY[2], RightBatY[3], Clock);
  Subtractor #(.width(5)) subtractor_1 (.a(BallX), .b(5'b00001), .out(subtractor_1_out));  // open: bin, bout
  Adder #(.width(5)) adder_1 (.a(BallX), .b(5'b00001), .out(adder_1_out));  // open: cin, cout
  Subtractor #(.width(5)) subtractor_2 (.a(BallY), .b(5'b00001), .out(subtractor_2_out));  // open: bin, bout
  Adder #(.width(5)) adder_2 (.a(BallY), .b(5'b00001), .out(adder_2_out));  // open: cin, cout
  Comparator #(.width(5), .mode("unsigned")) comparator_3 (
    .a({5{1'b0}}), .b(BallX), .eq(LeftWallReflect));  // open: gt, lt
  Comparator #(.width(5), .mode("unsigned")) comparator_4 (
    .a({5{1'b1}}), .b(BallX), .eq(RightWallReflect));  // open: gt, lt
  Multiplexer #(.width(5), .enable("false")) multiplexer_1 (
    .in0(subtractor_1_out), .in1(adder_1_out), .out(CoordToReflectX), .sel(VX));
  Multiplexer #(.width(5), .enable("false")) multiplexer_2 (
    .in0(subtractor_2_out), .in1(adder_2_out), .out(CoordToReflectY), .sel(VY));
  CheckReflection checkreflection_1 (
    .in_1(CoordToReflectX), .in_2(CoordToReflectY), .in_3(LeftBatY_2), .in_4(RigthBatY),
    .out_5(LeftBatReflect), .out_6(RightBatReflect));
  Comparator #(.width(5), .mode("unsigned")) comparator_5 (
    .a({5{1'b1}}), .b(BallY), .eq(TopWallReflect));  // open: gt, lt
  Comparator #(.width(5), .mode("unsigned")) comparator_6 (
    .a({5{1'b0}}), .b(BallY), .eq(BotWallReflect));  // open: gt, lt
  Register #(.width(5)) u_BallX (.D(CoordToReflectX), .Q(BallX), .clk(BT), .clr(EN_t));  // open: en
  Register #(.width(5)) u_BallY (.D(CoordToReflectY), .Q(BallY), .clk(BT), .clr(EN_t));  // open: en
  D_Flip_Flop u_VX (.clk(or_2_out), .D(VX_qn), .Q(VX), .Qn(VX_qn), .preset(EN_t));  // open: en, reset
  or or_2 (or_2_out, LeftWallReflect, RightWallReflect, LeftBatReflect, RightBatReflect);
  or or_3 (or_3_out, TopWallReflect, BotWallReflect);
  D_Flip_Flop u_VY (.clk(or_3_out), .D(VY_qn), .Q(VY), .Qn(VY_qn), .preset(EN_t));  // open: en, reset

  assign EN_2 = EN;

  // Other names for the same wires on the sheet: EN_In = EN; LeftBatYFin[4:0] = LeftBatY_2;
  //   RightBatYFin[4:0] = RigthBatY; RigthBatY_t[3:0] = RightBatY

  // Notes on the sheet:
  //   INPUT
  //   Left bat
  //   left wall
  //   right wall
  //   Bat Movement
  //   Score Count
  //   Right bat
  //   buffer_1 drives only 1 and floats otherwise
  //   buffer_2 drives only 1 and floats otherwise
  //   Ball Movement
  //   Ball Reflection
  //   OUTPUT
endmodule

module VideoChip (
  input  EN,
  input  [4:0] ballX,
  input  [4:0] ballY,
  input  [1:0] ID,
  input  [4:0] LeftBatY,
  input  [4:0] RightBatY,
  output [31:0] out_7,
  output EN_2,
  output [4:0] ballX_2,
  output [31:0] out_10,
  output [4:0] ballY_2,
  output [31:0] out_12,
  output [1:0] ID_2,
  output [4:0] LeftBatY_2,
  output [31:0] out_15,
  output [4:0] RightBatY_2,
  output [31:0] out_17,
  output [31:0] out_18,
  output [31:0] out_19,
  output [31:0] out_20
);

  wire comparator_1_eq;
  wire [31:0] demultiplexer_1_out0, FinalCol3, FinalCol4, LeftBat, RightBat;

  Pull_Resistor pull_resistor_1 (.node(EN));
  Pull_Resistor pull_resistor_2 (.node(ballX));
  Pull_Resistor pull_resistor_3 (.node(ballY));
  Pull_Resistor pull_resistor_4 (.node(ID));
  Pull_Resistor pull_resistor_5 (.node(LeftBatY));
  Pull_Resistor pull_resistor_6 (.node(RightBatY));
  Demultiplexer #(.select(5), .enable("false")) demultiplexer_1 (
    .out0(demultiplexer_1_out0[0]), .out1(demultiplexer_1_out0[1]), .out2(demultiplexer_1_out0[2]),
    .out3(demultiplexer_1_out0[3]), .out4(demultiplexer_1_out0[4]), .out5(demultiplexer_1_out0[5]),
    .out6(demultiplexer_1_out0[6]), .out7(demultiplexer_1_out0[7]), .out8(demultiplexer_1_out0[8]),
    .out9(demultiplexer_1_out0[9]), .out10(demultiplexer_1_out0[10]), .out11(demultiplexer_1_out0[11]),
    .out12(demultiplexer_1_out0[12]), .out13(demultiplexer_1_out0[13]), .out14(demultiplexer_1_out0[14]),
    .out15(demultiplexer_1_out0[15]), .out16(demultiplexer_1_out0[16]), .out17(demultiplexer_1_out0[17]),
    .out18(demultiplexer_1_out0[18]), .out19(demultiplexer_1_out0[19]), .out20(demultiplexer_1_out0[20]),
    .out21(demultiplexer_1_out0[21]), .out22(demultiplexer_1_out0[22]), .out23(demultiplexer_1_out0[23]),
    .out24(demultiplexer_1_out0[24]), .out25(demultiplexer_1_out0[25]), .out26(demultiplexer_1_out0[26]),
    .out27(demultiplexer_1_out0[27]), .out28(demultiplexer_1_out0[28]), .out29(demultiplexer_1_out0[29]),
    .out30(demultiplexer_1_out0[30]), .out31(demultiplexer_1_out0[31]), .in(EN), .sel(ballY));
  LeftBat leftbat_1 (.ID(ID), .LeftBatY(LeftBatY), .out_4(LeftBat), .EN(EN));
  RightBat rightbat_1 (.EN(EN), .ID(ID), .out_4(RightBat), .RightBatY(RightBatY));
  Demultiplexer #(.select(3), .width(32), .disabled(0)) demultiplexer_2 (
    .out0(out_7), .out1(out_10), .out2(out_12), .out3(FinalCol3), .out4(FinalCol4), .out5(out_18),
    .out6(out_19), .out7(out_20), .in(demultiplexer_1_out0), .sel(ballX[2:0]), .en(comparator_1_eq));
  Comparator #(.width(2), .mode("unsigned")) comparator_1 (
    .a(ballX[4:3]), .b(ID), .eq(comparator_1_eq));  // open: gt, lt
  assign out_15 = FinalCol3 | LeftBat;  // OR_Gate or_1, 32 bits wide
  assign out_17 = FinalCol4 | RightBat;  // OR_Gate or_2, 32 bits wide
  Adder #(.width(2)) adder_1 (.a(ID), .b(2'b01), .out(ID_2));  // open: cin, cout

  assign ballX_2 = ballX;
  assign ballY_2 = ballY;
  assign EN_2 = EN;
  assign LeftBatY_2 = LeftBatY;
  assign RightBatY_2 = RightBatY;

  // Other names for the same wires on the sheet: FinalCol0[31:0] = out_7; FinalCol1[31:0] = out_10;
  //   FinalCol2[31:0] = out_12; FinalCol5[31:0] = out_18; FinalCol6[31:0] = out_19; FinalCol7[31:0] = out_20

  // Notes on the sheet:
  //   INPUT
  //   OUTPUT
endmodule

module BatConstructor (
  input  [4:0] BatY,
  output [31:0] out_2
);

  wire [0:0] pull_resistor_2_node;
  wire [31:0] decoder_1_out31;
  wire [31:31] pull_resistor_1_node;

  Decoder #(.select(5), .disabled(0), .enable("false")) decoder_1 (
    .out0(decoder_1_out31[0]), .out1(decoder_1_out31[1]), .out2(decoder_1_out31[2]),
    .out3(decoder_1_out31[3]), .out4(decoder_1_out31[4]), .out5(decoder_1_out31[5]),
    .out6(decoder_1_out31[6]), .out7(decoder_1_out31[7]), .out8(decoder_1_out31[8]),
    .out9(decoder_1_out31[9]), .out10(decoder_1_out31[10]), .out11(decoder_1_out31[11]),
    .out12(decoder_1_out31[12]), .out13(decoder_1_out31[13]), .out14(decoder_1_out31[14]),
    .out15(decoder_1_out31[15]), .out16(decoder_1_out31[16]), .out17(decoder_1_out31[17]),
    .out18(decoder_1_out31[18]), .out19(decoder_1_out31[19]), .out20(decoder_1_out31[20]),
    .out21(decoder_1_out31[21]), .out22(decoder_1_out31[22]), .out23(decoder_1_out31[23]),
    .out24(decoder_1_out31[24]), .out25(decoder_1_out31[25]), .out26(decoder_1_out31[26]),
    .out27(decoder_1_out31[27]), .out28(decoder_1_out31[28]), .out29(decoder_1_out31[29]),
    .out30(decoder_1_out31[30]), .out31(decoder_1_out31[31]), .sel(BatY));
  Pull_Resistor pull_resistor_1 (.node(pull_resistor_1_node[31]));
  Pull_Resistor pull_resistor_2 (.node(pull_resistor_2_node[0]));
  assign out_2 = {pull_resistor_1_node[31], decoder_1_out31[31:1]} | decoder_1_out31 | {decoder_1_out31[30:0], pull_resistor_2_node[0]};  // OR_Gate or_1, 32 bits wide

  // Other names for the same wires on the sheet: Bat[31:0] = out_2

  // Notes on the sheet:
  //   INPUT
  //   OUTPUT
endmodule

module LeftBatMovement (
  input  EN,
  input  Clock,
  input  [3:0] LeftBatY,
  output [4:0] out_4
);

  wire and_1_out, and_2_out, comparator_1_eq, pull_resistor_2_node;
  wire [2:0] priority_encoder_1_out;
  wire [4:0] adder_1_out, multiplexer_1_out, subtractor_1_out;

  Adder #(.width(5)) adder_1 (.a(out_4), .b(5'b00001), .out(adder_1_out));  // open: cin, cout
  Subtractor #(.width(5)) subtractor_1 (.a(out_4), .b(5'b00001), .out(subtractor_1_out));  // open: bin, bout
  Priority_Encoder #(.disabled(0)) priority_encoder_1 (
    .in1(and_2_out), .in2(and_1_out), .in3(comparator_1_eq), .in4(pull_resistor_2_node),
    .out(priority_encoder_1_out));  // open: in0, in5, in6, in7, en_in, gs, en_out
  Pull_Resistor pull_resistor_1 (.node(priority_encoder_1_out));
  Multiplexer #(.select(3), .width(5), .enable("false")) multiplexer_1 (
    .in0(out_4), .in1(adder_1_out), .in2(subtractor_1_out), .in3(5'b11101), .in4(5'b00001),
    .out(multiplexer_1_out), .sel(priority_encoder_1_out));  // open: in5, in6, in7
  and and_1 (and_1_out, LeftBatY[0], LeftBatY[1], LeftBatY[2], LeftBatY[3]);
  and and_2 (and_2_out, ~LeftBatY[3], ~LeftBatY[2], ~LeftBatY[1], LeftBatY[0]);  // AND_Gate
  Register #(.width(5)) register_1 (.D(multiplexer_1_out), .Q(out_4), .clk(Clock), .clr(EN));  // open: en
  Comparator #(.width(5), .mode("unsigned")) comparator_1 (
    .a(adder_1_out), .b({5{1'b0}}), .eq(comparator_1_eq));  // open: gt, lt
  Pull_Resistor pull_resistor_2 (.node(pull_resistor_2_node));
  Comparator #(.width(5), .mode("unsigned")) comparator_2 (
    .a(subtractor_1_out), .b({5{1'b1}}), .eq(pull_resistor_2_node));  // open: gt, lt
  Pull_Resistor pull_resistor_3 (.node(comparator_1_eq));

  // Other names for the same wires on the sheet: LeftBatYFin[4:0] = out_4

  // Notes on the sheet:
  //   INPUT
  //   OUTPUT
endmodule

// LBC
module LeftBat (
  input  EN,
  input  [1:0] ID,
  input  [4:0] LeftBatY,
  output [31:0] out_4
);

  wire and_1_out, comparator_1_eq;
  wire [31:0] batconstructor_1_out_2;

  Comparator #(.width(2)) comparator_1 (.a(ID), .b(2'b00), .eq(comparator_1_eq));  // open: gt, lt
  and and_1 (and_1_out, comparator_1_eq, EN);
  assign out_4 = and_1_out ? batconstructor_1_out_2 : 32'bz;  // Controlled_Buffer controlled_buffer_1
  BatConstructor batconstructor_1 (.out_2(batconstructor_1_out_2), .BatY(LeftBatY));
  Pull_Resistor pull_resistor_1 (.node(out_4));

  // Other names for the same wires on the sheet: LeftBat[31:0] = out_4

  // Notes on the sheet:
  //   INPUT
  //   videochip №
  //   OUTPUT
endmodule

// RBC
module RightBat (
  input  EN,
  input  [1:0] ID,
  input  [4:0] RightBatY,
  output [31:0] out_4
);

  wire and_1_out, comparator_1_eq;
  wire [31:0] batconstructor_1_out_2;

  Comparator #(.width(2)) comparator_1 (.a(ID), .b(2'b11), .eq(comparator_1_eq));  // open: gt, lt
  and and_1 (and_1_out, comparator_1_eq, EN);
  BatConstructor batconstructor_1 (.out_2(batconstructor_1_out_2), .BatY(RightBatY));
  assign out_4 = and_1_out ? batconstructor_1_out_2 : 32'bz;  // Controlled_Buffer controlled_buffer_1
  Pull_Resistor pull_resistor_1 (.node(out_4));

  // Other names for the same wires on the sheet: RightBat[31:0] = out_4

  // Notes on the sheet:
  //   INPUT
  //   videochip №
  //   OUTPUT
endmodule

module BallDelay (
  input  Clock,
  input  in_2,
  input  in_3,
  input  in_4,
  output out_5
);

  wire comparator_1_eq, comparator_2_eq, comparator_3_eq, comparator_4_eq, controlled_buffer_1_out,
       controlled_buffer_2_out, controlled_buffer_3_out, d_ff_1_q, d_ff_1_qn, d_ff_2_q, d_ff_2_qn, d_ff_3_q,
       d_ff_3_qn;
  wire [1:0] priority_encoder_1_out;

  assign controlled_buffer_1_out = in_2 ? Clock : 1'bz;  // Controlled_Buffer controlled_buffer_1
  D_Flip_Flop d_ff_1 (
    .clk(controlled_buffer_1_out), .D(d_ff_1_qn), .Q(d_ff_1_q), .Qn(d_ff_1_qn));  // open: preset, en, reset
  assign controlled_buffer_2_out = in_3 ? d_ff_1_q : 1'bz;  // Controlled_Buffer controlled_buffer_2
  D_Flip_Flop d_ff_2 (
    .clk(controlled_buffer_2_out), .D(d_ff_2_qn), .Q(d_ff_2_q), .Qn(d_ff_2_qn));  // open: preset, en, reset
  Priority_Encoder #(.select(2)) priority_encoder_1 (
    .in0(Clock), .in1(in_2), .in2(in_3), .in3(in_4), .out(priority_encoder_1_out));  // open: gs, en_out, en_in
  D_Flip_Flop d_ff_3 (
    .clk(controlled_buffer_3_out), .D(d_ff_3_qn), .Q(d_ff_3_q), .Qn(d_ff_3_qn));  // open: preset, en, reset
  assign controlled_buffer_3_out = in_4 ? d_ff_2_q : 1'bz;  // Controlled_Buffer controlled_buffer_3
  Comparator #(.width(2)) comparator_1 (.a(priority_encoder_1_out), .b(2'b00), .eq(comparator_1_eq));  // open: gt, lt
  Comparator #(.width(2)) comparator_2 (.a(priority_encoder_1_out), .b(2'b01), .eq(comparator_2_eq));  // open: gt, lt
  Comparator #(.width(2)) comparator_3 (.a(priority_encoder_1_out), .b(2'b10), .eq(comparator_3_eq));  // open: gt, lt
  Comparator #(.width(2)) comparator_4 (.a(priority_encoder_1_out), .b(2'b11), .eq(comparator_4_eq));  // open: gt, lt
  Pull_Resistor pull_resistor_1 (.node(comparator_1_eq));
  Pull_Resistor pull_resistor_2 (.node(comparator_2_eq));
  Pull_Resistor pull_resistor_3 (.node(comparator_3_eq));
  Pull_Resistor pull_resistor_4 (.node(comparator_4_eq));
  Transistor #(.\type ("n")) transistor_1 (.in(Clock), .out(out_5), .gate(comparator_1_eq));
  Transistor #(.\type ("n")) transistor_2 (.in(d_ff_1_q), .out(out_5), .gate(comparator_2_eq));
  Transistor #(.\type ("n")) transistor_3 (.in(d_ff_2_q), .out(out_5), .gate(comparator_3_eq));
  Transistor #(.\type ("n")) transistor_4 (.in(d_ff_3_q), .out(out_5), .gate(comparator_4_eq));
  Pull_Resistor pull_resistor_5 (.node(out_5));

  // Other names for the same wires on the sheet: _1_1 = Clock; _1_2 = in_2; _1_4 = in_3; _1_8 = in_4; BT = out_5

  // Notes on the sheet:
  //   INPUT
  //   OUTPUT
  //   Ball Tick
endmodule

module CheckReflection (
  input  [4:0] in_1,
  input  [4:0] in_2,
  input  [4:0] in_3,
  input  [4:0] in_4,
  output out_5,
  output out_6
);

  wire comparator_1_gt, comparator_2_eq, comparator_3_gt, comparator_4_eq;
  wire [5:0] bitadder_1_out, bitadder_2_out, bitadder_3_out, bitadder_4_out;
  wire [31:0] batconstructor_1_out_2, batconstructor_2_out_2, decoder_1_out0, decoder_2_out0, xor_1_out,
       xor_2_out;

  Decoder #(.select(5), .disabled(0), .enable("false")) decoder_1 (
    .out0(decoder_1_out0[0]), .out1(decoder_1_out0[1]), .out2(decoder_1_out0[2]), .out3(decoder_1_out0[3]),
    .out4(decoder_1_out0[4]), .out5(decoder_1_out0[5]), .out6(decoder_1_out0[6]), .out7(decoder_1_out0[7]),
    .out8(decoder_1_out0[8]), .out9(decoder_1_out0[9]), .out10(decoder_1_out0[10]),
    .out11(decoder_1_out0[11]), .out12(decoder_1_out0[12]), .out13(decoder_1_out0[13]),
    .out14(decoder_1_out0[14]), .out15(decoder_1_out0[15]), .out16(decoder_1_out0[16]),
    .out17(decoder_1_out0[17]), .out18(decoder_1_out0[18]), .out19(decoder_1_out0[19]),
    .out20(decoder_1_out0[20]), .out21(decoder_1_out0[21]), .out22(decoder_1_out0[22]),
    .out23(decoder_1_out0[23]), .out24(decoder_1_out0[24]), .out25(decoder_1_out0[25]),
    .out26(decoder_1_out0[26]), .out27(decoder_1_out0[27]), .out28(decoder_1_out0[28]),
    .out29(decoder_1_out0[29]), .out30(decoder_1_out0[30]), .out31(decoder_1_out0[31]), .sel(in_2));
  Decoder #(.select(5), .disabled(0), .enable("false")) decoder_2 (
    .out0(decoder_2_out0[0]), .out1(decoder_2_out0[1]), .out2(decoder_2_out0[2]), .out3(decoder_2_out0[3]),
    .out4(decoder_2_out0[4]), .out5(decoder_2_out0[5]), .out6(decoder_2_out0[6]), .out7(decoder_2_out0[7]),
    .out8(decoder_2_out0[8]), .out9(decoder_2_out0[9]), .out10(decoder_2_out0[10]),
    .out11(decoder_2_out0[11]), .out12(decoder_2_out0[12]), .out13(decoder_2_out0[13]),
    .out14(decoder_2_out0[14]), .out15(decoder_2_out0[15]), .out16(decoder_2_out0[16]),
    .out17(decoder_2_out0[17]), .out18(decoder_2_out0[18]), .out19(decoder_2_out0[19]),
    .out20(decoder_2_out0[20]), .out21(decoder_2_out0[21]), .out22(decoder_2_out0[22]),
    .out23(decoder_2_out0[23]), .out24(decoder_2_out0[24]), .out25(decoder_2_out0[25]),
    .out26(decoder_2_out0[26]), .out27(decoder_2_out0[27]), .out28(decoder_2_out0[28]),
    .out29(decoder_2_out0[29]), .out30(decoder_2_out0[30]), .out31(decoder_2_out0[31]), .sel(in_1));
  BatConstructor batconstructor_1 (.out_2(batconstructor_1_out_2), .BatY(in_3));
  BatConstructor batconstructor_2 (.out_2(batconstructor_2_out_2), .BatY(in_4));
  BitAdder #(.width(32)) bitadder_1 (.in0(batconstructor_1_out_2), .out(bitadder_1_out));
  BitAdder #(.width(32)) bitadder_2 (.in0(xor_1_out), .out(bitadder_2_out));
  assign xor_1_out = batconstructor_1_out_2 ^ decoder_1_out0;  // XOR_Gate xor_1, 32 bits wide
  BitAdder #(.width(32)) bitadder_3 (.in0(batconstructor_2_out_2), .out(bitadder_3_out));
  BitAdder #(.width(32)) bitadder_4 (.in0(xor_2_out), .out(bitadder_4_out));
  assign xor_2_out = batconstructor_2_out_2 ^ decoder_1_out0;  // XOR_Gate xor_2, 32 bits wide
  Comparator #(.width(6), .mode("unsigned")) comparator_1 (
    .a(bitadder_1_out), .b(bitadder_2_out), .gt(comparator_1_gt));  // open: eq, lt
  Comparator #(.width(32), .mode("unsigned")) comparator_2 (
    .a(decoder_2_out0), .b(32'h8), .eq(comparator_2_eq));  // open: gt, lt
  Comparator #(.width(6), .mode("unsigned")) comparator_3 (
    .a(bitadder_3_out), .b(bitadder_4_out), .gt(comparator_3_gt));  // open: eq, lt
  Comparator #(.width(32), .mode("unsigned")) comparator_4 (
    .a(decoder_2_out0), .b(32'h10000000), .eq(comparator_4_eq));  // open: gt, lt
  and and_1 (out_5, comparator_1_gt, comparator_2_eq);
  and and_2 (out_6, comparator_3_gt, comparator_4_eq);

  // Other names for the same wires on the sheet: CoordToReflectX[4:0] = in_1; CoordToReflectY[4:0] = in_2;
  //   LeftBatReflect = out_5; LeftBatYFin[4:0] = in_3; RightBatReflect = out_6; RightBatYFin[4:0] = in_4

  // Notes on the sheet:
  //   INPUT
  //   OUTPUT
endmodule

module ScoreCounter (
  input  Flag,
  input  Reset,
  output [7:0] Score
);

  wire [7:0] counter_1_q;
  wire [7:4] divider_1_out, divider_1_rem;

  Counter #(.max('h63)) counter_1 (.Q(counter_1_q), .clk(Flag), .clr(Reset));  // open: load, D, count, carry
  Divider divider_1 (
    .a(counter_1_q), .b(8'ha), .out({divider_1_out, Score[3:0]}), .rem({divider_1_rem, Score[7:4]}));  // open: upper

  // Notes on the sheet:
  //   INPUT
  //   OUTPUT
endmodule
